// Logisim project EVM.circ as structural Verilog: 1 circuit, main circuit main
module main (
  input  C1,
  input  in_2,
  input  in_3,
  input  in_4,
  output out_5
);

  wire and_1_out, and_2_out, and_3_out;

  and and_1 (and_1_out, in_4, C1);
  and and_2 (and_2_out, in_3, C1);
  and and_3 (and_3_out, in_2, C1);
  or or_1 (out_5, and_1_out, and_2_out, and_3_out);
  LED led_1 (.in(out_5));

  // Notes on the sheet:
  //   VoterID
  //   C2
  //   C3
  //   CONFIRM
endmodule
